# Fritzing sketch lesson02-16 (saved by Fritzing 0.9.6b)
breadboards: 2

parts:
  J2 = Camdenboss CTB0158-2 [part_number=CTB0158-2 package=THT]
  SW2 = Slide_SW_micro_dpdt  # not connected
  BATT1 = LiPoly Battery (1300mAh)
  IC1 = DIP - 20 pins [package="DIP (Dual Inline) [THT]"]
  S1 = Tactile Switch Buttons - 12mm Square [package=tactile-pth-12mm]
  S2 = Tactile Switch Buttons - 12mm Square [package=tactile-pth-12mm]
  buz1 = Piezo Buzzer
  S3 = Tactile Switch Buttons - 12mm Square [package=tactile-pth-12mm]
  S4 = Tactile Switch Buttons - 12mm Square [package=tactile-pth-12mm]
  S5 = Momentary Switch [package=ksa_sealed_tac_switch]
  R9 = Resistor [tolerance=±5% power=0.25 resistance=330 package=THT]
  R10 = Resistor [tolerance=±5% power=0.25 resistance=330 package=THT]
  R11 = Resistor [tolerance=±5% power=0.25 resistance=330 package=THT]
  R13 = Resistor [tolerance=±5% power=0.25 resistance=330 package=THT]
  LED20 = LED - 5mm [color="Yellow (585nm)" current=30mA package="5 mm [THT]"]
  LED21 = LED - 5mm [color="Blue (470nm)" current=30mA package="5 mm [THT]"]
  LED23 = LED - 5mm [color="Red (633nm)" current=30mA package="5 mm [THT]"]
  LED22 = smd LED [color="Green (555nm)" current=30mA package="1206 [SMD]"]

nets:
  N1: J2.pin1, BATT1.negative, IC1.G#8
  N2: J2.pin2, BATT1.positive
  N3: IC1.25, buz1.pin_1
  N4: IC1.26, LED23.cathode
  N5: IC1.27, LED22.cathode
  N6: IC1.15, LED21.cathode
  N7: IC1.14, LED20.cathode
  N8: IC1.18, S1.1, S1.3
  N9: IC1.5, S2.1, S2.3
  N10: IC1.22, S3.2, S3.4
  N11: IC1.21, S4.2, S4.4
  N12: IC1.33, S5.3, S5.4
  N13: IC1.G#19, S1.2, S1.4, S2.2, S2.4, S3.1, S3.3, S4.1, S4.3, S5.1, S5.2, R9.Pin_1, R10.Pin_1, R11.Pin_1, R13.Pin_1
  N14: R9.Pin_0, LED23.anode
  N15: R10.Pin_0, LED22.anode
  N16: R11.Pin_0, LED21.anode
  N17: R13.Pin_0, LED20.anode

custom parts:
  Slide_SW_micro_dpdt: silver mico switch
  LiPoly Battery (1300mAh): Lithium Ion Polymer Battery (1300mAh)
  DIP - 20 pins: A DIP stand-in part for whatever IC you want. With 20 pins on a 300mil dual inline package (DIP) footprint.
  Tactile Switch Buttons - 12mm Square: Medium-sized clicky momentary switches are standard input "buttons" on electronic projects. These work best in a PCB but can be used on a solderless breadboard as shown in this tutorial. The pins are normally open (disconnected) and when the button is pressed they are momentarily closed. They come in a pack of 10, they're pretty handy so you'll want to keep them around. You can find an EAGLE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
  Piezo Buzzer: Part from https://www.nutsvolts.com/magazine/article/november2012_SmileysWorkshop modified to be .3 in spacing to match the adafruit buzzer 5V breadboard friendly part.
