# Fritzing sketch tinyPICO-01 (saved by Fritzing 0.9.6b)
breadboards: 2

parts:
  LED1 = smd LED [color="Red (633nm)" package="1206 [SMD]"]
  R3 = Resistor [tolerance=±5% resistance=330 package="2010 [SMD]"]
  J2 = Camdenboss CTB0158-2 [part_number=CTB0158-2 package=THT]
  SW2 = Slide_SW_micro_dpdt  # not connected
  BATT1 = LiPoly Battery (1300mAh)

nets:
  N1: LED1.cathode, R3.Pin_1
  N2: R3.Pin_0, J2.pin1, BATT1.negative
  N3: J2.pin2, BATT1.positive

custom parts:
  Slide_SW_micro_dpdt: silver mico switch
  LiPoly Battery (1300mAh): Lithium Ion Polymer Battery (1300mAh)
