# Fritzing sketch tinyPICO-11 (saved by Fritzing 0.9.6b)
breadboards: 2

parts:
  LED1 = smd LED [color="Red (633nm)" package="1206 [SMD]"]
  R3 = Resistor [tolerance=±5% resistance=330 package="2010 [SMD]"]
  J2 = Camdenboss CTB0158-2 [part_number=CTB0158-2 package=THT]
  SW2 = Slide_SW_micro_dpdt  # not connected
  BATT1 = LiPoly Battery (1300mAh)
  IC1 = DIP - 20 pins [package="DIP (Dual Inline) [THT]"]
  S1 = Tactile Switch Buttons - 12mm Square [package=tactile-pth-12mm]
  S2 = Tactile Switch Buttons - 12mm Square [package=tactile-pth-12mm]
  buz1 = Piezo Buzzer

nets:
  N1: LED1.cathode, R3.Pin_0
  N2: LED1.anode, IC1.25
  N3: R3.Pin_1, IC1.G#19, S1.2, S1.4, S2.2, S2.4
  N4: J2.pin1, BATT1.negative, IC1.G#8, buz1.pin_1
  N5: J2.pin2, BATT1.positive
  N6: IC1.15, buz1.pin_2
  N7: IC1.5, S1.1, S1.3
  N8: IC1.22, S2.1, S2.3

custom parts:
  Slide_SW_micro_dpdt: silver mico switch
  LiPoly Battery (1300mAh): Lithium Ion Polymer Battery (1300mAh)
  DIP - 20 pins: A DIP stand-in part for whatever IC you want. With 20 pins on a 300mil dual inline package (DIP) footprint.
  Tactile Switch Buttons - 12mm Square: Medium-sized clicky momentary switches are standard input "buttons" on electronic projects. These work best in a PCB but can be used on a solderless breadboard as shown in this tutorial. The pins are normally open (disconnected) and when the button is pressed they are momentarily closed. They come in a pack of 10, they're pretty handy so you'll want to keep them around. You can find an EAGLE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
  Piezo Buzzer: Part from https://www.nutsvolts.com/magazine/article/november2012_SmileysWorkshop modified to be .3 in spacing to match the adafruit buzzer 5V breadboard friendly part.
