# Fritzing sketch tinyPICO-14 (saved by Fritzing 0.9.6b)
breadboards: 2

parts:
  R3 = Resistor [tolerance=±5% resistance=330 package="2010 [SMD]"]
  J2 = Camdenboss CTB0158-2 [part_number=CTB0158-2 package=THT]
  SW2 = Slide_SW_micro_dpdt  # not connected
  BATT1 = LiPoly Battery (1300mAh)
  IC1 = DIP - 20 pins [package="DIP (Dual Inline) [THT]"]
  S1 = Tactile Switch Buttons - 12mm Square [package=tactile-pth-12mm]
  S2 = Tactile Switch Buttons - 12mm Square [package=tactile-pth-12mm]
  buz1 = Piezo Buzzer
  R4 = Resistor [tolerance=±5% resistance=330 package="2010 [SMD]"]
  LED2 = smd LED [color="Green (570nm)" package="1206 [SMD]"]
  R5 = Resistor [tolerance=±5% resistance=330 package="2010 [SMD]"]
  LED3 = smd LED [color="Yellow (595nm)" package="1206 [SMD]"]
  LED4 = smd LED [color="Red (633nm)" package="1206 [SMD]"]
  S3 = Tactile Switch Buttons - 12mm Square [package=tactile-pth-12mm]
  S4 = Tactile Switch Buttons - 12mm Square [package=tactile-pth-12mm]
  S5 = Momentary Switch [package=ksa_sealed_tac_switch]

nets:
  N1: R3.Pin_0, LED4.cathode
  N2: R3.Pin_1, IC1.G#19, S1.2, S1.4, S2.2, S2.4, R4.Pin_1, R5.Pin_1, S3.2, S3.4, S4.2, S4.4, S5.2
  N3: J2.pin1, BATT1.negative, IC1.G#8, buz1.pin_1
  N4: J2.pin2, BATT1.positive
  N5: IC1.25, LED4.anode
  N6: IC1.26, LED3.anode
  N7: IC1.27, LED2.anode
  N8: IC1.15, buz1.pin_2
  N9: IC1.5, S1.1, S1.3
  N10: IC1.22, S2.1, S2.3
  N11: IC1.21, S3.1, S3.3
  N12: IC1.32, S4.1, S4.3
  N13: IC1.33, S5.4
  N14: R4.Pin_0, LED3.cathode
  N15: LED2.cathode, R5.Pin_0

custom parts:
  Slide_SW_micro_dpdt: silver mico switch
  LiPoly Battery (1300mAh): Lithium Ion Polymer Battery (1300mAh)
  DIP - 20 pins: A DIP stand-in part for whatever IC you want. With 20 pins on a 300mil dual inline package (DIP) footprint.
  Tactile Switch Buttons - 12mm Square: Medium-sized clicky momentary switches are standard input "buttons" on electronic projects. These work best in a PCB but can be used on a solderless breadboard as shown in this tutorial. The pins are normally open (disconnected) and when the button is pressed they are momentarily closed. They come in a pack of 10, they're pretty handy so you'll want to keep them around. You can find an EAGLE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
  Piezo Buzzer: Part from https://www.nutsvolts.com/magazine/article/november2012_SmileysWorkshop modified to be .3 in spacing to match the adafruit buzzer 5V breadboard friendly part.
