# Fritzing sketch tinyPICO-final (saved by Fritzing 0.9.6b)
breadboards: 2

parts:
  LED1 = smd LED [color="Red (633nm)" package="1206 [SMD]"]
  LED2 = smd LED [color="Yellow (595nm)" package="1206 [SMD]"]
  LED3 = smd LED [color="Green (570nm)" package="1206 [SMD]"]
  R1 = Resistor [tolerance=±0.05% resistance=330 package="2010 [SMD]"]
  R2 = Resistor [tolerance=±5% resistance=330 package="2010 [SMD]"]
  R3 = Resistor [tolerance=±5% resistance=330 package="2010 [SMD]"]
  TinyPICO = DIP - 20 pins [chip_label="Tiny PICO" package="DIP (Dual Inline) [THT]"]
  J2 = Camdenboss CTB0158-2 [part_number=CTB0158-2 package=THT]
  SW2 = Slide_SW_micro_dpdt  # not connected
  S1 = Momentary Switch [package=ksa_sealed_tac_switch]
  BATT1 = LiPoly Battery (1300mAh)
  S2 = Tactile Switch Buttons - 12mm Square [package=tactile-pth-12mm]  # not connected
  S3 = Tactile Switch Buttons - 12mm Square [package=tactile-pth-12mm]  # not connected
  S4 = Tactile Switch Buttons - 12mm Square [package=tactile-pth-12mm]  # not connected
  S5 = Tactile Switch Buttons - 12mm Square [package=tactile-pth-12mm]  # not connected
  buz1 = Piezo Buzzer

nets:
  N1: LED1.cathode, R3.Pin_0
  N2: LED1.anode, TinyPICO.25
  N3: LED2.cathode, R2.Pin_0
  N4: LED2.anode, TinyPICO.26
  N5: LED3.cathode, R1.Pin_0
  N6: LED3.anode, TinyPICO.27
  N7: R1.Pin_1, R2.Pin_1, R3.Pin_1
  N8: TinyPICO.15, buz1.pin_2
  N9: TinyPICO.G#8, J2.pin1, BATT1.negative, buz1.pin_1
  N10: TinyPICO.33, S1.2
  N11: TinyPICO.G#19, S1.4
  N12: J2.pin2, BATT1.positive

custom parts:
  DIP - 20 pins: A DIP stand-in part for whatever IC you want. With 20 pins on a 300mil dual inline package (DIP) footprint.
  Slide_SW_micro_dpdt: silver mico switch
  LiPoly Battery (1300mAh): Lithium Ion Polymer Battery (1300mAh)
  Tactile Switch Buttons - 12mm Square: Medium-sized clicky momentary switches are standard input "buttons" on electronic projects. These work best in a PCB but can be used on a solderless breadboard as shown in this tutorial. The pins are normally open (disconnected) and when the button is pressed they are momentarily closed. They come in a pack of 10, they're pretty handy so you'll want to keep them around. You can find an EAGLE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
  Piezo Buzzer: Part from https://www.nutsvolts.com/magazine/article/november2012_SmileysWorkshop modified to be .3 in spacing to match the adafruit buzzer 5V breadboard friendly part.
